# Fritzing sketch kitchen lights (saved by Fritzing 0.9.3b)
breadboards: 1

parts:
  U1 = ESP32S-HiLetgo [part_number=ESP32S-HiLetgo]
  Part1 = Logic Level Converter
  R1 = PHOTOCELL [package=photocell]
  PIR1 = PIR_sensor
  R2 = Resistor [tolerance=±5% resistance=10k package="1206 [SMD]"]
  U2 = SK6812 RGBW LED Strip
  S4 = Toggle Switch [package=THT]
  S5 = Toggle Switch [package=THT]
  S6 = Momentary Switch [package=ksa_sealed_tac_switch]
  U3 = SK6812 RGBW LED Strip
  S7 = Momentary Switch [package=ksa_sealed_tac_switch]

nets:
  N1: U1.3.3, Part1.LV, R1.P$1, PIR1.connector1
  N2: U1.GPIO32, R1.P$2, R2.Pin_0
  N3: U1.GPIO14, PIR1.connector2
  N4: U1.GPIO12, S4.L1
  GND: U1.GND, Part1.GND, PIR1.connector3, R2.Pin_1, U2.GND#0, S4.COM, S5.COM, S6.3, U3.GND#0, S7.3
  N5: U1.GPIO13, S5.L1
  +5V: U1.VIN, Part1.HV, U2.+5V, U3.+5V
  N6: U1.GPIO15, S7.1
  N7: U1.GPIO16, Part1.TX_LV
  N8: U1.GPIO17, Part1.TX2_LV
  N9: U1.GPIO5, S6.1
  N10: Part1.TX_HV, U2.Din, U2.GND#3
  N11: Part1.TX2_HV, U3.Din, U3.GND#3

custom parts:
  ESP32S-HiLetgo: HiLetgo ESP-WROOM-32 ESP32 ESP-32S Development Board 2.4GHz Dual-Mode WiFi + Bluetooth Dual Cores Microcontroller The ESP32 integrated with Antenna switches, RF Balun, power amplifiers, low-noise amplifiers, filters, and management modules, and the entire solution occupies the least area of PCB. 2.4 GHz Wi-Fi plus Bluetooth dual-mode chip, with TSMC Ultra-low power consumption 40nm technology,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
  SK6812 RGBW LED Strip: SK6812 RGBW Strip
